# Fritzing sketch led_to_bag (saved by Fritzing 0.9.3b)
breadboards: 1

parts:
  Pulsante1 = Arduino Uno (Rev3)
  Led1Verde = LED - 3mm [color="Green (570nm)" package="3 mm [THT]"]
  Led3Verde = LED - 3mm [color="Green (570nm)" package="3 mm [THT]"]
  LED1 = LED - 3mm [color="White (4500K)" package="3 mm [THT]"]
  LED2 = LED - 3mm [color="Red (633nm)" package="3 mm [THT]"]
  R1 = Resistor [tolerance=±5% resistance=330 package=THT]
  R2 = Resistor [tolerance=±5% resistance=330 package=THT]
  R3 = Resistor [tolerance=±5% resistance=330 package=THT]
  R4 = Resistor [tolerance=±5% resistance=330 package=THT]
  R7 = Rotary Potentiometer (Small) [maximum_resistance=100kΩ package=THT]
  S1 = Pushbutton [package="[SMD]"]
  S2 = Pushbutton [package="[SMD]"]
  R8 = Resistor [tolerance=±2% resistance=1k package="2512 [SMD]"]
  R6 = Resistor [tolerance=±5% resistance=330 package=THT]
  Led2Verde = LED - 3mm [color="Green (570nm)" package="3 mm [THT]"]
  R9 = Resistor [tolerance=±2% resistance=1k package="2512 [SMD]"]

nets:
  N1: Pulsante1.A0, R7.wiper
  N2: Pulsante1.D8, R6.Pin_1
  N3: Pulsante1.D9_PWM, R3.Pin_1
  N4: Pulsante1.D12/MISO, S1.Pin_1, S1.Pin_2, R9.Pin_0
  N5: Pulsante1.D13/SCK, S2.Pin_1, S2.Pin_2, R8.Pin_0
  N6: Pulsante1.D2, R2.Pin_1
  N7: Pulsante1.D4, R4.Pin_1
  N8: Pulsante1.D7, R1.Pin_1
  N9: Pulsante1.5V, R7.leg2, S1.Pin_3, S1.Pin_4, S2.Pin_3, S2.Pin_4
  N10: Pulsante1.GND, Led1Verde.cathode, Led3Verde.cathode, LED1.cathode, LED2.cathode, R7.leg1, R8.Pin_1, Led2Verde.cathode, R9.Pin_1
  N11: Led1Verde.anode, R2.Pin_0
  N12: Led3Verde.anode, R1.Pin_0
  N13: LED1.anode, R3.Pin_0
  N14: LED2.anode, R6.Pin_0
  N15: R4.Pin_0, Led2Verde.anode

notes:
  Il led bianco è l'unico collegato ad un pin PWM perchè richiesto che effettui una pulsazione, cosa possibile solo con un Pwm o un'uscita analogica
