# Fritzing sketch Prototipo2 (saved by Fritzing 0.9.3b)
breadboards: 1

parts:
  Componente1 = Arduino Uno (Rev3)
  R1 = Rotary Potentiometer (Small) [maximum_resistance=100kΩ package=THT]
  LED1 = LED - 3mm [color="Red (633nm)" package="3 mm [THT]"]
  R2 = Resistor [tolerance=±5% resistance=220 package="0402 [SMD]"]
  R3 = Resistor [tolerance=±5% resistance=220 package="0402 [SMD]"]
  S1 = Pushbutton [package="[THT]"]
  S2 = Pushbutton [package="[THT]"]
  S3 = Pushbutton [package="[THT]"]
  R4 = Resistor [tolerance=±5% resistance=10k package="0402 [SMD]"]
  R5 = Resistor [tolerance=±5% resistance=10k package="0402 [SMD]"]
  R6 = Resistor [tolerance=±5% resistance=10k package="0402 [SMD]"]
  X1 = Sonar
  J1 = Basic Servo
  LED2 = LED - 3mm [color="Red (633nm)" package="3 mm [THT]"]
  Sensore_PIR_HC-SR502 = HC-SR501 Body Sensor Module

nets:
  N1: Componente1.A0, R1.wiper
  N2: Componente1.D8, S3.Pin_3, S3.Pin_4, R5.Pin_1
  N3: Componente1.D9_PWM, S2.Pin_3, S2.Pin_4, R4.Pin_1
  N4: Componente1.D10_PWM/SS, S1.Pin_3, S1.Pin_4, R6.Pin_1
  N5: Componente1.D2, Sensore_PIR_HC-SR502.OUT
  N6: Componente1.D3_PWM, X1.SCL
  N7: Componente1.D4, X1.SDA
  N8: Componente1.D5_PWM, LED1.anode
  N9: Componente1.D6_PWM, J1.pulse
  VCC: Componente1.5V, R1.leg1, S1.Pin_1, S1.Pin_2, S2.Pin_1, S2.Pin_2, S3.Pin_1, S3.Pin_2, X1.+5, J1.vcc, Sensore_PIR_HC-SR502.VCC
  GND: Componente1.GND, R1.leg2, R2.Pin_0, R3.Pin_0, R4.Pin_0, R5.Pin_0, R6.Pin_0, X1.GND, J1.gnd, Sensore_PIR_HC-SR502.GND
  N10: LED1.cathode, R3.Pin_1
  N11: R2.Pin_1, LED2.cathode

custom parts:
  Sonar: Devantech SRF08 sonar range-finder. I2C interface. Other Devantech sonars similar
  HC-SR501 Body Sensor Module: Pyroelectric Infrared PIR Motion Sensor Detector Module
